# Fritzing sketch coro_min_test (saved by Fritzing 0.9.3b)
breadboards: 1

parts:
  R1 = Resistor [tolerance=±5% resistance=220 package=THT]
  LED2 = smd LED [color="Red (633nm)" package="0805 [SMD]"]

nets:
  N1: R1.Pin_0, LED2.anode

notes:
  K22F J2/14 (Earth)
  K22F J2/6 (PTB16)
